// Logisim project CRC_Module_all.circ as structural Verilog
module ModuloCRCALL (
  input  MD__selects_the_behaviour_of_the_chip,
  input  Clock,
  input  Reset,
  input  Line_IN,
  output Line_OUT,
  output BUSY
);
endmodule

// do_xor
module Do_XOR (
  input  B,
  input  A,
  input  E,
  output C
);

  wire and_1_out;

  and and_1 (and_1_out, A, E);
  xor xor_1 (C, B, and_1_out);
endmodule
